// Logisim project ALUpj3.circ as structural Verilog
module main (
);

  ALU alu_1 ();  // open: in_1, in_2, in_3, in_4, out_7, out_8, in_5, in_6
  Register_File register_file_1 ();  // open: Reloj, in_13, out_16, _4, in_8, _3, in_9, _2, in_10, _1, in_11, _0, in_12, Input_de_todos, in_14, Output_high, out_17
endmodule

module ALU (
  input  [31:0] in_1,
  input  [31:0] in_2,
  input  [31:0] in_3,
  input  [31:0] in_4,
  input  [4:0] in_5,
  input  [3:0] in_6,
  output [31:0] out_7,
  output [31:0] out_8
);

  wire adder_2_cout, subtractor_2_bout;
  wire [31:0] adder_1_out, adder_2_out, and_1_out, and_2_out, or_1_out, or_2_out, shift_left_1_salida_high,
       shift_left_1_salida_low, shift_right_1_salida_high, shift_right_1_salida_low, shifter_1_out,
       shifter_2_out, shifter_3_out, shifter_4_out, subtractor_1_out, subtractor_2_out, xor_1_out, xor_2_out;

  Adder #(.width(32)) adder_1 (.a(in_1), .b(in_3), .out(adder_1_out), .cin(adder_2_cout));  // open: cout
  Subtractor #(.width(32)) subtractor_1 (
    .a(in_1), .b(in_3), .out(subtractor_1_out), .bin(subtractor_2_bout));  // open: bout
  assign and_1_out = in_1 & in_3;  // AND_Gate and_1, 32 bits wide
  assign or_1_out = in_1 | in_3;  // OR_Gate or_1, 32 bits wide
  assign xor_1_out = in_1 ^ in_3;  // XOR_Gate xor_1, 32 bits wide
  Shift_Left shift_left_1 (
    .High(in_1), .Corrimiento(in_5), .Low(in_4), .Salida_high(shift_left_1_salida_high),
    .Salida_low(shift_left_1_salida_low));
  Shift_right shift_right_1 (
    .High(in_1), .Corrimiento(in_5), .Low(in_2), .Salida_high(shift_right_1_salida_high),
    .Salida_Low(shift_right_1_salida_low));
  Shifter #(.width(32), .shift("ar")) shifter_1 (.out(shifter_1_out));  // open: in, dist
  Shifter #(.width(32), .shift("rr")) shifter_2 (.out(shifter_2_out));  // open: in, dist
  Adder #(.width(32)) adder_2 (.a(in_2), .b(in_4), .out(adder_2_out), .cout(adder_2_cout));  // open: cin
  Subtractor #(.width(32)) subtractor_2 (
    .a(in_2), .b(in_4), .out(subtractor_2_out), .bout(subtractor_2_bout));  // open: bin
  assign and_2_out = in_2 & in_4;  // AND_Gate and_2, 32 bits wide
  assign or_2_out = in_2 | in_4;  // OR_Gate or_2, 32 bits wide
  assign xor_2_out = in_2 ^ in_4;  // XOR_Gate xor_2, 32 bits wide
  Shifter #(.width(32), .shift("ar")) shifter_3 (.out(shifter_3_out));  // open: in, dist
  Shifter #(.width(32), .shift("rr")) shifter_4 (.out(shifter_4_out));  // open: in, dist
  Multiplexer #(.select(4), .width(32)) multiplexer_1 (
    .in0(adder_1_out), .in1(subtractor_1_out), .in2(and_1_out), .in3(or_1_out), .in4(xor_1_out),
    .in5(shift_left_1_salida_high), .in6(shift_right_1_salida_high), .in7(shifter_1_out),
    .in8(shifter_2_out), .in9({32{1'b0}}), .in10({32{1'b0}}), .in11({32{1'b0}}), .in12({32{1'b0}}),
    .in13({32{1'b0}}), .in14({32{1'b0}}), .in15({32{1'b0}}), .out(out_7), .sel(in_6), .en(1'b1));
  Multiplexer #(.select(4), .width(32)) multiplexer_2 (
    .in0(adder_2_out), .in1(subtractor_2_out), .in2(and_2_out), .in3(or_2_out), .in4(xor_2_out),
    .in5(shift_left_1_salida_low), .in6(shift_right_1_salida_low), .in7(shifter_3_out), .in8(shifter_4_out),
    .in9({32{1'b0}}), .in10({32{1'b0}}), .in11({32{1'b0}}), .in12({32{1'b0}}), .in13({32{1'b0}}),
    .in14({32{1'b0}}), .in15({32{1'b0}}), .out(out_8), .sel(in_6), .en(1'b1));

  // Other names for the same wires on the sheet: Control[3:0] = in_6; Input_High_1[31:0] = in_1;
  //   Input_high_2[31:0] = in_3; Input_low_1[31:0] = in_2; Input_low_2[31:0] = in_4; Offset_shift[4:0] = in_5;
  //   Output_high[31:0] = out_7; Output_low[31:0] = out_8
endmodule

module Memory_Manager_instrucciones (
  input  [23:0] in_1,
  input  [31:0] in_2,
  input  in_3,
  input  clear,
  input  in_5
);

  wire ckl;

  Clock clock_1 (.out(ckl));
  RAM #(.addrWidth(24), .dataWidth(32)) ram_1 (.addr(in_1), .data(in_2), .sel(in_3), .clk(ckl), .ld(in_5), .clr(clear));
endmodule

module Register_File (
  input  _4,
  input  _3,
  input  _2,
  input  _1,
  input  _0,
  input  Reloj,
  input  [31:0] Input_de_todos,
  input  in_8,
  input  in_9,
  input  in_10,
  input  in_11,
  input  in_12,
  input  in_13,
  input  [31:0] in_14,
  output [31:0] Output_high,
  output [4:0] out_16,
  output [31:0] out_17
);

  wire and_1_out, and_2_out, and_3_out, and_4_out, and_5_out, and_6_out, and_7_out, and_8_out, and_9_out,
       and_10_out, and_11_out, and_12_out, and_13_out, and_14_out, and_15_out, and_16_out, and_17_out,
       and_18_out, and_19_out, and_20_out, and_21_out, and_22_out, and_23_out, and_24_out, and_25_out,
       and_26_out, and_27_out, and_28_out, and_29_out, and_30_out, and_31_out, and_32_out, and_33_out,
       and_34_out, and_35_out, and_36_out, and_37_out, and_38_out, and_39_out, and_40_out, and_41_out,
       and_42_out, and_43_out, and_44_out, and_45_out, and_46_out, and_47_out, and_48_out, and_49_out,
       and_50_out, and_51_out, and_52_out, and_53_out, and_54_out, and_55_out, and_56_out, and_57_out,
       and_58_out, and_59_out, and_60_out, and_61_out, and_62_out, and_63_out, and_64_out, not_1_out,
       not_2_out, not_3_out, not_4_out, not_5_out, not_6_out, not_7_out, not_8_out, not_9_out, not_10_out,
       not_11_out, not_12_out, not_13_out, not_14_out, not_15_out, not_16_out, not_17_out, not_18_out,
       not_19_out, not_20_out, not_21_out, not_22_out, not_23_out, not_24_out, not_25_out, not_26_out,
       not_27_out, not_28_out, not_29_out, not_30_out, not_31_out, not_32_out, not_33_out, not_34_out,
       not_35_out, not_36_out, not_37_out, not_38_out, not_39_out, not_40_out, not_41_out, not_42_out,
       not_43_out, not_44_out, not_45_out, not_46_out, not_47_out, not_48_out, not_49_out, not_50_out,
       not_51_out, not_52_out, not_53_out, not_54_out, not_55_out, not_56_out, not_57_out, not_58_out,
       not_59_out, not_60_out, not_61_out, not_62_out, not_63_out, not_64_out, not_65_out, not_66_out,
       not_67_out, not_68_out, not_69_out, not_70_out, not_71_out, not_72_out, not_73_out, not_74_out,
       not_75_out, not_76_out, not_77_out, not_78_out, not_79_out, not_80_out, not_81_out, not_82_out,
       not_83_out, not_84_out, not_85_out, not_86_out, not_87_out, not_88_out, not_89_out, not_90_out,
       not_91_out, not_92_out, not_93_out, not_94_out, not_95_out, not_96_out, not_97_out, not_98_out,
       not_99_out, not_100_out, not_101_out, not_102_out, not_103_out, not_104_out, not_105_out, not_106_out,
       not_107_out, not_108_out, not_109_out, not_110_out, not_111_out, not_112_out, not_113_out,
       not_114_out, not_115_out, not_116_out, not_117_out, not_118_out, not_119_out, not_120_out,
       not_121_out, not_122_out, not_123_out, not_124_out, not_125_out, not_126_out, not_127_out,
       not_128_out, not_129_out, not_130_out, not_131_out, not_132_out, not_133_out, not_134_out,
       not_135_out, not_136_out, not_137_out, not_138_out, not_139_out, not_140_out, not_141_out,
       not_142_out, not_143_out, not_144_out, not_145_out, not_146_out, not_147_out, not_148_out,
       not_149_out, not_150_out, not_151_out, not_152_out, not_153_out, not_154_out, not_155_out,
       not_156_out, not_157_out, not_158_out, not_159_out, not_160_out;
  wire [31:0] undriven, undriven_2, undriven_3, undriven_4, undriven_5, undriven_6, undriven_7, undriven_8,
       undriven_9, undriven_10, x0_2_q, x0_q, x1_2_q, x1_q, x3_2_q, x3_q, x4_2_q, x4_3_q, x4_4_q, x4_5_q,
       x4_6_q, x4_q, x6_2_q, x6_q, x7_2_q, x7_q, x8_2_q, x8_q, x9_2_q, x9_3_q, x9_4_q, x9_q, x11_2_q, x11_q,
       x12_2_q, x12_q, x13_2_q, x13_q, x14_2_q, x14_q, x15_2_q, x15_q, x16_2_q, x16_q, x17_2_q, x17_q,
       x18_2_q, x18_q, x19_2_q, x19_q, x20_2_q, x20_q, x21_2_q, x21_3_q, x21_4_q, x21_q, x23_2_q, x23_3_q,
       x23_4_q, x23_q, x25_2_q, x25_q, x26_2_q, x26_q, x27_2_q, x27_q, x28_2_q, x28_q, x29_2_q, x29_q,
       x30_2_q, x30_q, x31_2_q, x31_q;

  not not_1 (not_1_out, _1);
  not not_2 (not_2_out, _2);
  not not_3 (not_3_out, _3);
  not not_4 (not_4_out, _4);
  not not_5 (not_5_out, _0);
  not not_6 (not_6_out, _2);
  not not_7 (not_7_out, _3);
  not not_8 (not_8_out, _4);
  not not_9 (not_9_out, _2);
  not not_10 (not_10_out, _3);
  not not_11 (not_11_out, _4);
  not not_12 (not_12_out, _0);
  not not_13 (not_13_out, _1);
  not not_14 (not_14_out, _3);
  not not_15 (not_15_out, _4);
  not not_16 (not_16_out, _1);
  not not_17 (not_17_out, _3);
  not not_18 (not_18_out, _4);
  not not_19 (not_19_out, _0);
  not not_20 (not_20_out, _3);
  not not_21 (not_21_out, _4);
  not not_22 (not_22_out, _3);
  not not_23 (not_23_out, _4);
  not not_24 (not_24_out, _0);
  not not_25 (not_25_out, _1);
  not not_26 (not_26_out, _2);
  not not_27 (not_27_out, _4);
  not not_28 (not_28_out, _1);
  not not_29 (not_29_out, _2);
  not not_30 (not_30_out, _4);
  not not_31 (not_31_out, _0);
  not not_32 (not_32_out, _2);
  not not_33 (not_33_out, _4);
  not not_34 (not_34_out, _2);
  not not_35 (not_35_out, _4);
  not not_36 (not_36_out, _0);
  not not_37 (not_37_out, _1);
  not not_38 (not_38_out, _4);
  not not_39 (not_39_out, _1);
  not not_40 (not_40_out, _4);
  not not_41 (not_41_out, _0);
  not not_42 (not_42_out, _4);
  not not_43 (not_43_out, _4);
  not not_44 (not_44_out, _0);
  not not_45 (not_45_out, _1);
  not not_46 (not_46_out, _2);
  not not_47 (not_47_out, _3);
  not not_48 (not_48_out, _1);
  not not_49 (not_49_out, _2);
  not not_50 (not_50_out, _3);
  not not_51 (not_51_out, _0);
  not not_52 (not_52_out, _2);
  not not_53 (not_53_out, _3);
  not not_54 (not_54_out, _2);
  not not_55 (not_55_out, _3);
  not not_56 (not_56_out, _0);
  not not_57 (not_57_out, _1);
  not not_58 (not_58_out, _3);
  not not_59 (not_59_out, _1);
  not not_60 (not_60_out, _3);
  not not_61 (not_61_out, _0);
  not not_62 (not_62_out, _3);
  not not_63 (not_63_out, _3);
  not not_64 (not_64_out, _0);
  not not_65 (not_65_out, _1);
  not not_66 (not_66_out, _2);
  not not_67 (not_67_out, _1);
  not not_68 (not_68_out, _2);
  not not_69 (not_69_out, _0);
  not not_70 (not_70_out, _2);
  not not_71 (not_71_out, _2);
  not not_72 (not_72_out, _0);
  not not_73 (not_73_out, _1);
  not not_74 (not_74_out, _1);
  not not_75 (not_75_out, _0);
  not not_76 (not_76_out, _0);
  not not_77 (not_77_out, _1);
  not not_78 (not_78_out, _2);
  not not_79 (not_79_out, _3);
  not not_80 (not_80_out, _4);
  not not_81 (not_81_out, in_11);
  not not_82 (not_82_out, in_10);
  not not_83 (not_83_out, in_9);
  not not_84 (not_84_out, in_8);
  not not_85 (not_85_out, in_12);
  not not_86 (not_86_out, in_10);
  not not_87 (not_87_out, in_9);
  not not_88 (not_88_out, in_8);
  not not_89 (not_89_out, in_10);
  not not_90 (not_90_out, in_9);
  not not_91 (not_91_out, in_8);
  not not_92 (not_92_out, in_12);
  not not_93 (not_93_out, in_11);
  not not_94 (not_94_out, in_9);
  not not_95 (not_95_out, in_8);
  not not_96 (not_96_out, in_11);
  not not_97 (not_97_out, in_9);
  not not_98 (not_98_out, in_8);
  not not_99 (not_99_out, in_12);
  not not_100 (not_100_out, in_9);
  not not_101 (not_101_out, in_8);
  not not_102 (not_102_out, in_9);
  not not_103 (not_103_out, in_8);
  not not_104 (not_104_out, in_12);
  not not_105 (not_105_out, in_11);
  not not_106 (not_106_out, in_10);
  not not_107 (not_107_out, in_8);
  not not_108 (not_108_out, in_11);
  not not_109 (not_109_out, in_10);
  not not_110 (not_110_out, in_8);
  not not_111 (not_111_out, in_12);
  not not_112 (not_112_out, in_10);
  not not_113 (not_113_out, in_8);
  not not_114 (not_114_out, in_10);
  not not_115 (not_115_out, in_8);
  not not_116 (not_116_out, in_12);
  not not_117 (not_117_out, in_11);
  not not_118 (not_118_out, in_8);
  not not_119 (not_119_out, in_11);
  not not_120 (not_120_out, in_8);
  not not_121 (not_121_out, in_12);
  not not_122 (not_122_out, in_8);
  not not_123 (not_123_out, in_8);
  not not_124 (not_124_out, in_12);
  not not_125 (not_125_out, in_11);
  not not_126 (not_126_out, in_10);
  not not_127 (not_127_out, in_9);
  not not_128 (not_128_out, in_11);
  not not_129 (not_129_out, in_10);
  not not_130 (not_130_out, in_9);
  not not_131 (not_131_out, in_12);
  not not_132 (not_132_out, in_10);
  not not_133 (not_133_out, in_9);
  not not_134 (not_134_out, in_10);
  not not_135 (not_135_out, in_9);
  not not_136 (not_136_out, in_12);
  not not_137 (not_137_out, in_11);
  not not_138 (not_138_out, in_9);
  not not_139 (not_139_out, in_11);
  not not_140 (not_140_out, in_9);
  not not_141 (not_141_out, in_12);
  not not_142 (not_142_out, in_9);
  not not_143 (not_143_out, in_9);
  not not_144 (not_144_out, in_12);
  not not_145 (not_145_out, in_11);
  not not_146 (not_146_out, in_10);
  not not_147 (not_147_out, in_11);
  not not_148 (not_148_out, in_10);
  not not_149 (not_149_out, in_12);
  not not_150 (not_150_out, in_10);
  not not_151 (not_151_out, in_10);
  not not_152 (not_152_out, in_12);
  not not_153 (not_153_out, in_11);
  not not_154 (not_154_out, in_11);
  not not_155 (not_155_out, in_12);
  not not_156 (not_156_out, in_12);
  not not_157 (not_157_out, in_11);
  not not_158 (not_158_out, in_10);
  not not_159 (not_159_out, in_9);
  not not_160 (not_160_out, in_8);
  and and_1 (and_1_out, _0, not_1_out, not_2_out, not_3_out, not_4_out);
  and and_2 (and_2_out, not_5_out, _1, not_6_out, not_7_out, not_8_out);
  and and_3 (and_3_out, _0, _1, not_9_out, not_10_out, not_11_out);
  and and_4 (and_4_out, not_12_out, not_13_out, _2, not_14_out, not_15_out);
  and and_5 (and_5_out, _0, not_16_out, _2, not_17_out, not_18_out);
  and and_6 (and_6_out, not_19_out, _1, _2, not_20_out, not_21_out);
  and and_7 (and_7_out, _0, _1, _2, not_22_out, not_23_out);
  and and_8 (and_8_out, not_24_out, not_25_out, not_26_out, _3, not_27_out);
  and and_9 (and_9_out, _0, not_28_out, not_29_out, _3, not_30_out);
  and and_10 (and_10_out, not_31_out, _1, not_32_out, _3, not_33_out);
  and and_11 (and_11_out, _0, _1, not_34_out, _3, not_35_out);
  and and_12 (and_12_out, not_36_out, not_37_out, _2, _3, not_38_out);
  and and_13 (and_13_out, _0, not_39_out, _2, _3, not_40_out);
  and and_14 (and_14_out, not_41_out, _1, _2, _3, not_42_out);
  and and_15 (and_15_out, _0, _1, _2, _3, not_43_out);
  and and_16 (and_16_out, not_44_out, not_45_out, not_46_out, not_47_out, _4);
  and and_17 (and_17_out, _0, not_48_out, not_49_out, not_50_out, _4);
  and and_18 (and_18_out, not_51_out, _1, not_52_out, not_53_out, _4);
  and and_19 (and_19_out, _0, _1, not_54_out, not_55_out, _4);
  and and_20 (and_20_out, not_56_out, not_57_out, _2, not_58_out, _4);
  and and_21 (and_21_out, _0, not_59_out, _2, not_60_out, _4);
  and and_22 (and_22_out, not_61_out, _1, _2, not_62_out, _4);
  and and_23 (and_23_out, _0, _1, _2, not_63_out, _4);
  and and_24 (and_24_out, not_64_out, not_65_out, not_66_out, _3, _4);
  and and_25 (and_25_out, _0, not_67_out, not_68_out, _3, _4);
  and and_26 (and_26_out, not_69_out, _1, not_70_out, _3, _4);
  and and_27 (and_27_out, _0, _1, not_71_out, _3, _4);
  and and_28 (and_28_out, not_72_out, not_73_out, _2, _3, _4);
  and and_29 (and_29_out, _0, not_74_out, _2, _3, _4);
  and and_30 (and_30_out, not_75_out, _1, _2, _3, _4);
  and and_31 (and_31_out, _0, _1, _2, _3, _4);
  and and_32 (and_32_out, not_76_out, not_77_out, not_78_out, not_79_out, not_80_out);
  and and_33 (and_33_out, in_12, not_81_out, not_82_out, not_83_out, not_84_out);
  and and_34 (and_34_out, not_85_out, in_11, not_86_out, not_87_out, not_88_out);
  and and_35 (and_35_out, in_12, in_11, not_89_out, not_90_out, not_91_out);
  and and_36 (and_36_out, not_92_out, not_93_out, in_10, not_94_out, not_95_out);
  and and_37 (and_37_out, in_12, not_96_out, in_10, not_97_out, not_98_out);
  and and_38 (and_38_out, not_99_out, in_11, in_10, not_100_out, not_101_out);
  and and_39 (and_39_out, in_12, in_11, in_10, not_102_out, not_103_out);
  and and_40 (and_40_out, not_104_out, not_105_out, not_106_out, in_9, not_107_out);
  and and_41 (and_41_out, in_12, not_108_out, not_109_out, in_9, not_110_out);
  and and_42 (and_42_out, not_111_out, in_11, not_112_out, in_9, not_113_out);
  and and_43 (and_43_out, in_12, in_11, not_114_out, in_9, not_115_out);
  and and_44 (and_44_out, not_116_out, not_117_out, in_10, in_9, not_118_out);
  and and_45 (and_45_out, in_12, not_119_out, in_10, in_9, not_120_out);
  and and_46 (and_46_out, not_121_out, in_11, in_10, in_9, not_122_out);
  and and_47 (and_47_out, in_12, in_11, in_10, in_9, not_123_out);
  and and_48 (and_48_out, not_124_out, not_125_out, not_126_out, not_127_out, in_8);
  and and_49 (and_49_out, in_12, not_128_out, not_129_out, not_130_out, in_8);
  and and_50 (and_50_out, not_131_out, in_11, not_132_out, not_133_out, in_8);
  and and_51 (and_51_out, in_12, in_11, not_134_out, not_135_out, in_8);
  and and_52 (and_52_out, not_136_out, not_137_out, in_10, not_138_out, in_8);
  and and_53 (and_53_out, in_12, not_139_out, in_10, not_140_out, in_8);
  and and_54 (and_54_out, not_141_out, in_11, in_10, not_142_out, in_8);
  and and_55 (and_55_out, in_12, in_11, in_10, not_143_out, in_8);
  and and_56 (and_56_out, not_144_out, not_145_out, not_146_out, in_9, in_8);
  and and_57 (and_57_out, in_12, not_147_out, not_148_out, in_9, in_8);
  and and_58 (and_58_out, not_149_out, in_11, not_150_out, in_9, in_8);
  and and_59 (and_59_out, in_12, in_11, not_151_out, in_9, in_8);
  and and_60 (and_60_out, not_152_out, not_153_out, in_10, in_9, in_8);
  and and_61 (and_61_out, in_12, not_154_out, in_10, in_9, in_8);
  and and_62 (and_62_out, not_155_out, in_11, in_10, in_9, in_8);
  and and_63 (and_63_out, in_12, in_11, in_10, in_9, in_8);
  and and_64 (and_64_out, not_156_out, not_157_out, not_158_out, not_159_out, not_160_out);
  Register #(.width(32)) x1 (.D(Input_de_todos), .en(and_1_out), .Q(x1_q), .clk(Reloj));  // open: clr
  Register #(.width(32)) x4 (.D(Input_de_todos), .en(and_2_out), .Q(x4_q), .clk(Reloj));  // open: clr
  Register #(.width(32)) x3 (.D(Input_de_todos), .en(and_3_out), .Q(x3_q), .clk(Reloj));  // open: clr
  Register #(.width(32)) x4_2 (.D(Input_de_todos), .en(and_4_out), .Q(x4_2_q), .clk(Reloj));  // open: clr
  Register #(.width(32)) x4_3 (.D(Input_de_todos), .en(and_5_out), .Q(x4_3_q), .clk(Reloj));  // open: clr
  Register #(.width(32)) x6 (.D(Input_de_todos), .en(and_6_out), .Q(x6_q), .clk(Reloj));  // open: clr
  Register #(.width(32)) x7 (.D(Input_de_todos), .en(and_7_out), .Q(x7_q), .clk(Reloj));  // open: clr
  Register #(.width(32)) x8 (.D(Input_de_todos), .en(and_8_out), .Q(x8_q), .clk(Reloj));  // open: clr
  Register #(.width(32)) x9 (.D(Input_de_todos), .en(and_9_out), .Q(x9_q), .clk(Reloj));  // open: clr
  Register #(.width(32)) x9_2 (.D(Input_de_todos), .en(and_10_out), .Q(x9_2_q), .clk(Reloj));  // open: clr
  Register #(.width(32)) x11 (.D(Input_de_todos), .en(and_11_out), .Q(x11_q), .clk(Reloj));  // open: clr
  Register #(.width(32)) x12 (.D(Input_de_todos), .en(and_12_out), .Q(x12_q), .clk(Reloj));  // open: clr
  Register #(.width(32)) x13 (.D(Input_de_todos), .en(and_13_out), .Q(x13_q), .clk(Reloj));  // open: clr
  Register #(.width(32)) x14 (.D(Input_de_todos), .en(and_14_out), .Q(x14_q), .clk(Reloj));  // open: clr
  Register #(.width(32)) x15 (.D(Input_de_todos), .en(and_15_out), .Q(x15_q), .clk(Reloj));  // open: clr
  Register #(.width(32)) x16 (.D(undriven), .en(and_16_out), .Q(x16_q), .clk(Reloj));  // open: clr
  Register #(.width(32)) x17 (.D(undriven_2), .en(and_17_out), .Q(x17_q), .clk(Reloj));  // open: clr
  Register #(.width(32)) x18 (.D(Input_de_todos), .en(and_18_out), .Q(x18_q), .clk(Reloj));  // open: clr
  Register #(.width(32)) x19 (.D(Input_de_todos), .en(and_19_out), .Q(x19_q), .clk(Reloj));  // open: clr
  Register #(.width(32)) x20 (.D(Input_de_todos), .en(and_20_out), .Q(x20_q), .clk(Reloj));  // open: clr
  Register #(.width(32)) x21 (.D(Input_de_todos), .en(and_21_out), .Q(x21_q), .clk(Reloj));  // open: clr
  Register #(.width(32)) x21_2 (.D(Input_de_todos), .en(and_22_out), .Q(x21_2_q), .clk(Reloj));  // open: clr
  Register #(.width(32)) x23 (.D(Input_de_todos), .en(and_23_out), .Q(x23_q), .clk(Reloj));  // open: clr
  Register #(.width(32)) x23_2 (.D(Input_de_todos), .en(and_24_out), .Q(x23_2_q), .clk(Reloj));  // open: clr
  Register #(.width(32)) x25 (.D(Input_de_todos), .en(and_25_out), .Q(x25_q), .clk(Reloj));  // open: clr
  Register #(.width(32)) x26 (.D(Input_de_todos), .en(and_26_out), .Q(x26_q), .clk(Reloj));  // open: clr
  Register #(.width(32)) x27 (.D(Input_de_todos), .en(and_27_out), .Q(x27_q), .clk(Reloj));  // open: clr
  Register #(.width(32)) x28 (.D(Input_de_todos), .en(and_28_out), .Q(x28_q), .clk(Reloj));  // open: clr
  Register #(.width(32)) x29 (.D(Input_de_todos), .en(and_29_out), .Q(x29_q), .clk(Reloj));  // open: clr
  Register #(.width(32)) x30 (.D(Input_de_todos), .en(and_30_out), .Q(x30_q), .clk(Reloj));  // open: clr
  Register #(.width(32)) x31 (.D(Input_de_todos), .en(and_31_out), .Q(x31_q), .clk(Reloj));  // open: clr
  Register #(.width(32)) x0 (.D(Input_de_todos), .en(and_32_out), .Q(x0_q), .clk(Reloj));  // open: clr
  Register #(.width(32)) x1_2 (.D(in_14), .en(and_33_out), .Q(x1_2_q), .clk(in_13));  // open: clr
  Register #(.width(32)) x4_4 (.D(in_14), .en(and_34_out), .Q(x4_4_q), .clk(in_13));  // open: clr
  Register #(.width(32)) x3_2 (.D(in_14), .en(and_35_out), .Q(x3_2_q), .clk(in_13));  // open: clr
  Register #(.width(32)) x4_5 (.D(in_14), .en(and_36_out), .Q(x4_5_q), .clk(in_13));  // open: clr
  Register #(.width(32)) x4_6 (.D(in_14), .en(and_37_out), .Q(x4_6_q), .clk(in_13));  // open: clr
  Register #(.width(32)) x6_2 (.D(in_14), .en(and_38_out), .Q(x6_2_q), .clk(in_13));  // open: clr
  Register #(.width(32)) x7_2 (.D(in_14), .en(and_39_out), .Q(x7_2_q), .clk(in_13));  // open: clr
  Register #(.width(32)) x8_2 (.D(in_14), .en(and_40_out), .Q(x8_2_q), .clk(in_13));  // open: clr
  Register #(.width(32)) x9_3 (.D(in_14), .en(and_41_out), .Q(x9_3_q), .clk(in_13));  // open: clr
  Register #(.width(32)) x9_4 (.D(in_14), .en(and_42_out), .Q(x9_4_q), .clk(in_13));  // open: clr
  Register #(.width(32)) x11_2 (.D(in_14), .en(and_43_out), .Q(x11_2_q), .clk(in_13));  // open: clr
  Register #(.width(32)) x12_2 (.D(in_14), .en(and_44_out), .Q(x12_2_q), .clk(in_13));  // open: clr
  Register #(.width(32)) x13_2 (.D(in_14), .en(and_45_out), .Q(x13_2_q), .clk(in_13));  // open: clr
  Register #(.width(32)) x14_2 (.D(in_14), .en(and_46_out), .Q(x14_2_q), .clk(in_13));  // open: clr
  Register #(.width(32)) x15_2 (.D(in_14), .en(and_47_out), .Q(x15_2_q), .clk(in_13));  // open: clr
  Register #(.width(32)) x16_2 (.D(undriven_4), .en(and_48_out), .Q(x16_2_q), .clk(in_13));  // open: clr
  Register #(.width(32)) x17_2 (.D(undriven_3), .en(and_49_out), .Q(x17_2_q), .clk(in_13));  // open: clr
  Register #(.width(32)) x18_2 (.D(in_14), .en(and_50_out), .Q(x18_2_q), .clk(in_13));  // open: clr
  Register #(.width(32)) x19_2 (.D(in_14), .en(and_51_out), .Q(x19_2_q), .clk(in_13));  // open: clr
  Register #(.width(32)) x20_2 (.D(in_14), .en(and_52_out), .Q(x20_2_q), .clk(in_13));  // open: clr
  Register #(.width(32)) x21_3 (.D(in_14), .en(and_53_out), .Q(x21_3_q), .clk(in_13));  // open: clr
  Register #(.width(32)) x21_4 (.D(in_14), .en(and_54_out), .Q(x21_4_q), .clk(in_13));  // open: clr
  Register #(.width(32)) x23_3 (.D(in_14), .en(and_55_out), .Q(x23_3_q), .clk(in_13));  // open: clr
  Register #(.width(32)) x23_4 (.D(in_14), .en(and_56_out), .Q(x23_4_q), .clk(in_13));  // open: clr
  Register #(.width(32)) x25_2 (.D(in_14), .en(and_57_out), .Q(x25_2_q), .clk(in_13));  // open: clr
  Register #(.width(32)) x26_2 (.D(in_14), .en(and_58_out), .Q(x26_2_q), .clk(in_13));  // open: clr
  Register #(.width(32)) x27_2 (.D(in_14), .en(and_59_out), .Q(x27_2_q), .clk(in_13));  // open: clr
  Register #(.width(32)) x28_2 (.D(in_14), .en(and_60_out), .Q(x28_2_q), .clk(in_13));  // open: clr
  Register #(.width(32)) x29_2 (.D(in_14), .en(and_61_out), .Q(x29_2_q), .clk(in_13));  // open: clr
  Register #(.width(32)) x30_2 (.D(in_14), .en(and_62_out), .Q(x30_2_q), .clk(in_13));  // open: clr
  Register #(.width(32)) x31_2 (.D(in_14), .en(and_63_out), .Q(x31_2_q), .clk(in_13));  // open: clr
  Register #(.width(32)) x0_2 (.D(in_14), .en(and_64_out), .Q(x0_2_q), .clk(in_13));  // open: clr
  Multiplexer #(.select(5), .width(32)) multiplexer_1 (
    .in0(x0_q), .in1(x1_q), .in2(undriven_7), .in3(undriven_8), .in4(x4_2_q), .in5(x4_3_q), .in6(x6_q),
    .in7(undriven_5), .in8(x8_q), .in9(x9_q), .in10(x9_2_q), .in11(x11_q), .in12(x12_q), .in13(x13_q),
    .in14(x14_q), .in15(x15_q), .in16(x16_q), .in17(x17_q), .in18(x18_q), .in19(x19_q), .in20(x20_q),
    .in21(x21_q), .in22(x21_2_q), .in23(x23_q), .in24(x23_2_q), .in25(x25_q), .in26(x26_q), .in27(x27_q),
    .in28(x28_q), .in29(x29_q), .in30(x30_q), .in31(x31_q), .out(Output_high), .sel({_4, _3, _2, _1, _0}));  // open: en
  Multiplexer #(.select(5), .width(32)) multiplexer_2 (
    .in0(x0_2_q), .in1(x1_2_q), .in2(undriven_9), .in3(undriven_10), .in4(x4_5_q), .in5(x4_6_q),
    .in6(x6_2_q), .in7(undriven_6), .in8(x8_2_q), .in9(x9_3_q), .in10(x9_4_q), .in11(x11_2_q),
    .in12(x12_2_q), .in13(x13_2_q), .in14(x14_2_q), .in15(x15_2_q), .in16(x16_2_q), .in17(x17_2_q),
    .in18(x18_2_q), .in19(x19_2_q), .in20(x20_2_q), .in21(x21_3_q), .in22(x21_4_q), .in23(x23_3_q),
    .in24(x23_4_q), .in25(x25_2_q), .in26(x26_2_q), .in27(x27_2_q), .in28(x28_2_q), .in29(x29_2_q),
    .in30(x30_2_q), .in31(x31_2_q), .out(out_17), .sel({in_8, in_9, in_10, in_11, in_12}));  // open: en

  assign out_16 = {in_8, in_9, in_10, in_11, in_12};
endmodule

module Program_Counter (
  input  [31:0] Instruccion,
  input  in_2,
  input  in_3,
  output [31:0] out_4
);

  wire clock_1_out;
  wire [31:0] adder_1_out, adder_2_out, multiplexer_1_out;

  Adder #(.width(32)) adder_1 (.a(out_4), .b(32'h4), .out(adder_1_out));  // open: cin, cout
  Adder #(.width(32)) adder_2 (.a(Instruccion), .b(out_4), .out(adder_2_out));  // open: cin, cout
  Multiplexer #(.width(32), .enable("false")) multiplexer_1 (
    .in0(adder_1_out), .in1(adder_2_out), .out(multiplexer_1_out), .sel(in_2));
  Register #(.width(32)) register_1 (.D(multiplexer_1_out), .Q(out_4), .clk(clock_1_out), .clr(in_3));  // open: en
  Clock clock_1 (.out(clock_1_out));
endmodule

module Decoder (
  input  [31:0] Instruccion
);

  wire not_1_out, not_2_out, not_3_out, not_4_out, not_5_out, not_6_out, not_7_out, not_8_out, not_9_out,
       not_10_out, not_11_out, not_12_out, not_13_out;

  not not_1 (not_1_out, Instruccion[25]);
  not not_2 (not_2_out, Instruccion[26]);
  // AND_Gate I_Add__etc has open pins: in0=Instruccion[27], in1=not_2_out, in2=not_1_out, in3=not_4_out, in4=Instruccion[23], out=open
  not not_3 (not_3_out, Instruccion[27]);
  not not_4 (not_4_out, Instruccion[24]);
  not not_5 (not_5_out, Instruccion[25]);
  // AND_Gate R_add__etc has open pins: in0=not_3_out, in1=Instruccion[26], in2=not_5_out, in3=Instruccion[24], in4=Instruccion[23], out=open
  not not_6 (not_6_out, Instruccion[25]);
  not not_7 (not_7_out, Instruccion[27]);
  not not_8 (not_8_out, Instruccion[23]);
  // AND_Gate R_and__etc has open pins: in0=not_7_out, in1=Instruccion[26], in2=not_6_out, in3=Instruccion[24], in4=not_8_out, out=open
  not not_9 (not_9_out, Instruccion[25]);
  // AND_Gate R_shifts has open pins: in0=Instruccion[27], in1=Instruccion[26], in2=not_9_out, in3=Instruccion[24], in4=not_10_out, out=open
  not not_10 (not_10_out, Instruccion[23]);
  not not_11 (not_11_out, Instruccion[23]);
  not not_12 (not_12_out, Instruccion[25]);
  not not_13 (not_13_out, Instruccion[26]);
  // AND_Gate R_mov has open pins: in0=Instruccion[27], in1=not_13_out, in2=not_12_out, in3=Instruccion[24], in4=not_11_out, out=open
  // AND_Gate and_1 is placed but not wired
endmodule

module Shift_Left (
  input  [31:0] High,
  input  [4:0] Corrimiento,
  input  [31:0] Low,
  output [31:0] Salida_high,
  output [31:0] Salida_low
);

  wire [4:0] subtractor_1_out;
  wire [31:0] or_1_out, shifter_1_out, shifter_2_out;

  Subtractor #(.width(5)) subtractor_1 (.a({5{1'b1}}), .b(Corrimiento), .out(subtractor_1_out));  // open: bin, bout
  Shifter #(.width(32)) shifter_1 (.in(High), .\dist (Corrimiento), .out(shifter_1_out));
  assign or_1_out = Low | {32{1'b0}};  // OR_Gate or_1, 32 bits wide
  Shifter #(.width(32), .shift("lr")) shifter_2 (.in(or_1_out), .\dist (subtractor_1_out), .out(shifter_2_out));
  assign Salida_high = shifter_1_out | shifter_2_out;  // OR_Gate or_2, 32 bits wide
  Shifter #(.width(32)) shifter_3 (.in(Low), .\dist (Corrimiento), .out(Salida_low));
endmodule

module Shift_right (
  input  [31:0] High,
  input  [4:0] Corrimiento,
  input  [31:0] Low,
  output [31:0] Salida_high,
  output [31:0] Salida_Low
);

  wire [4:0] subtractor_1_out;
  wire [31:0] or_1_out, shifter_1_out, shifter_3_out;

  Subtractor #(.width(5)) subtractor_1 (.a({5{1'b1}}), .b(Corrimiento), .out(subtractor_1_out));  // open: bin, bout
  assign or_1_out = High | {32{1'b0}};  // OR_Gate or_1, 32 bits wide
  Shifter #(.width(32), .shift("lr")) shifter_1 (.in(Low), .\dist (Corrimiento), .out(shifter_1_out));
  Shifter #(.width(32), .shift("lr")) shifter_2 (.in(High), .\dist (Corrimiento), .out(Salida_high));
  Shifter #(.width(32)) shifter_3 (.in(or_1_out), .\dist (subtractor_1_out), .out(shifter_3_out));
  assign Salida_Low = shifter_3_out | shifter_1_out;  // OR_Gate or_2, 32 bits wide
endmodule

module Prueba_registro (
  input  [3:0] in_1,
  input  in_2,
  output [3:0] out_3
);

  Register #(.width(4)) register_1 (.D(in_1), .Q(out_3), .clk(in_2));  // open: en, clr
endmodule
